// Logisim project 4 -BIT RIGHT SHIFT.circ as structural Verilog: 1 circuit, main circuit main
module main (
  input  D1
);

  wire CLK_out, d_ff_1_q, d_ff_2_q, d_ff_3_q, d_ff_4_q;

  Clock CLK (.out(CLK_out));
  D_Flip_Flop d_ff_1 (.clk(CLK_out), .D(D1), .Q(d_ff_1_q));  // open: Qn, preset, en, reset
  LED Q1 (.in(d_ff_1_q));
  D_Flip_Flop d_ff_2 (.clk(CLK_out), .D(d_ff_1_q), .Q(d_ff_2_q));  // open: Qn, preset, en, reset
  LED Q2 (.in(d_ff_2_q));
  D_Flip_Flop d_ff_3 (.clk(CLK_out), .D(d_ff_2_q), .Q(d_ff_3_q));  // open: Qn, preset, en, reset
  LED Q3 (.in(d_ff_3_q));
  D_Flip_Flop d_ff_4 (.clk(CLK_out), .D(d_ff_3_q), .Q(d_ff_4_q));  // open: Qn, preset, en, reset
  LED Q4 (.in(d_ff_4_q));
endmodule
