// Logisim project 4 bit parallel rigister.circ as structural Verilog: 1 circuit, main circuit main
module main (
  input  Serial_Data_in,
  input  clear,
  output Q1,
  output Q2,
  output Q3,
  output Q4
);

  wire CLK_out;

  Clock CLK (.out(CLK_out));
  D_Flip_Flop d_ff_1 (.clk(CLK_out), .D(Serial_Data_in), .Q(Q1), .reset(clear));  // open: Qn, preset, en
  D_Flip_Flop d_ff_2 (.clk(CLK_out), .D(Q1), .Q(Q2), .reset(clear));  // open: Qn, preset, en
  D_Flip_Flop d_ff_3 (.clk(CLK_out), .D(Q2), .Q(Q3), .reset(clear));  // open: Qn, preset, en
  D_Flip_Flop d_ff_4 (.clk(CLK_out), .D(Q3), .Q(Q4), .reset(clear));  // open: Qn, preset, en
endmodule
