// Logisim project D flip flop.circ as structural Verilog: 1 circuit, main circuit main
module main (
  input  D,
  output Q,
  output nQ
);

  wire clock_1_out, nand_1_out, nand_2_out, nand_3_out;

  Clock clock_1 (.out(clock_1_out));
  nand nand_1 (nand_1_out, D, clock_1_out);
  nand nand_2 (nand_2_out, clock_1_out, nand_3_out);
  nand nand_3 (nand_3_out, D, D);
  nand nand_4 (Q, nand_1_out, nQ);
  nand nand_5 (nQ, Q, nand_2_out);
endmodule
