// Logisim project Decade Counter.circ as structural Verilog: 2 circuits, main circuit main
module main (
  output Q0,
  output Q1,
  output Q2,
  output Q3
);

  wire clock_1_out, LD1_out, TC2_out, TC3_out;

  Clock clock_1 (.out(clock_1_out));
  JK jk_1 (.J(1'b1), .CK(clock_1_out), .K(1'b1), .nPR(1'b1), .nCLR(LD1_out), .Q(Q0));  // open: nQ
  JK jk_2 (.J(Q0), .CK(clock_1_out), .K(Q0), .nPR(1'b1), .nCLR(LD1_out), .Q(Q1));  // open: nQ
  and TC2 (TC2_out, Q0, Q1);
  and TC3 (TC3_out, TC2_out, Q2);
  JK jk_3 (.J(TC2_out), .CK(clock_1_out), .K(TC2_out), .nPR(1'b1), .nCLR(LD1_out), .Q(Q2));  // open: nQ
  JK jk_4 (.J(TC3_out), .CK(clock_1_out), .K(TC3_out), .nPR(1'b1), .nCLR(LD1_out), .Q(Q3));  // open: nQ
  nand LD1 (LD1_out, Q1, Q3);
  Hex_Digit_Display hex_digit_display_1 (.value({Q3, Q2, Q1, Q0}));  // open: dp

  // Notes on the sheet:
  //   ~PR
  //   ~CLR
endmodule

module JK (
  input  nPR,
  input  J,
  input  CK,
  input  K,
  input  nCLR,
  output Q,
  output nQ
);

  wire not_1_out, not_2_out;

  J_K_Flip_Flop j_k_ff_1 (.J(J), .clk(CK), .K(K), .Q(Q), .Qn(nQ), .preset(not_2_out), .en(1'b1), .reset(not_1_out));
  not not_1 (not_1_out, nCLR);
  not not_2 (not_2_out, nPR);
endmodule
