// Logisim project JK FLIP FLOP.circ as structural Verilog: 1 circuit, main circuit main
module main (
  input  J,
  input  K,
  output Q,
  output nQ
);

  wire clock_1_out, G1_out, G2_out;

  Clock clock_1 (.out(clock_1_out));
  nand G1 (G1_out, nQ, J, clock_1_out);
  nand G2 (G2_out, clock_1_out, K, Q);
  nand G3 (Q, G1_out, nQ);
  nand G4 (nQ, Q, G2_out);
endmodule
