// Logisim project t flip flop.circ as structural Verilog: 1 circuit, main circuit main
module main (
  input  in_1,
  input  in_2,
  output Q1,
  output Q2
);

  wire AND_2_out, AND_out, CLK_out;

  Clock CLK (.out(CLK_out));
  and AND (AND_out, Q2, in_1, CLK_out);
  and AND_2 (AND_2_out, CLK_out, in_2, Q1);
  nand NAND (Q1, AND_out, Q2);
  nand NAND_2 (Q2, Q1, AND_2_out);
endmodule
